// Logisim project regfile.circ as structural Verilog: 1 circuit, main circuit regfile
module regfile (
  input  [4:0] rs1,
  input  [4:0] rs2,
  input  [4:0] rd,
  input  [31:0] Write_Data,
  input  RegWEn,
  input  clk,
  output [31:0] ra,
  output [31:0] sp,
  output [31:0] t0,
  output [31:0] t1,
  output [31:0] t2,
  output [31:0] s0,
  output [31:0] s1,
  output [31:0] a0,
  output [31:0] Read_Data_1,
  output [31:0] Read_Data_2
);

  wire write_en0, write_en1, write_en2, write_en3, write_en4, write_en5, write_en6, write_en7, write_en8,
       write_en9, write_en10, write_en11, write_en12, write_en13, write_en14, write_en15, write_en16,
       write_en17, write_en18, write_en19, write_en20, write_en21, write_en22, write_en23, write_en24,
       write_en25, write_en26, write_en27, write_en28, write_en29, write_en30, write_en31;
  wire [31:0] x0_out, x3_out, x4_out, x11_out, x12_out, x13_out, x14_out, x15_out, x16_out, x17_out, x18_out,
       x19_out, x20_out, x21_out, x22_out, x23_out, x24_out, x25_out, x26_out, x27_out, x28_out, x29_out,
       x30_out, x31_out;

  Register #(.width(32)) register_1 (.D({32{1'b0}}), .en(write_en0), .clk(clk), .Q(x0_out));  // open: clr
  Register #(.width(32)) register_2 (.D(Write_Data), .en(write_en1), .clk(clk), .Q(ra));  // open: clr
  Register #(.width(32)) register_3 (.D(Write_Data), .en(write_en2), .clk(clk), .Q(sp));  // open: clr
  Register #(.width(32)) register_4 (.D(Write_Data), .en(write_en3), .clk(clk), .Q(x3_out));  // open: clr
  Register #(.width(32)) register_5 (.D(Write_Data), .en(write_en4), .clk(clk), .Q(x4_out));  // open: clr
  Register #(.width(32)) register_6 (.D(Write_Data), .en(write_en5), .clk(clk), .Q(t0));  // open: clr
  Register #(.width(32)) register_7 (.D(Write_Data), .en(write_en6), .clk(clk), .Q(t1));  // open: clr
  Register #(.width(32)) register_8 (.D(Write_Data), .en(write_en7), .clk(clk), .Q(t2));  // open: clr
  Register #(.width(32)) register_9 (.D(Write_Data), .en(write_en8), .clk(clk), .Q(s0));  // open: clr
  Register #(.width(32)) register_10 (.D(Write_Data), .en(write_en9), .clk(clk), .Q(s1));  // open: clr
  Register #(.width(32)) register_11 (.D(Write_Data), .en(write_en10), .clk(clk), .Q(a0));  // open: clr
  Register #(.width(32)) register_12 (.D(Write_Data), .en(write_en11), .clk(clk), .Q(x11_out));  // open: clr
  Register #(.width(32)) register_13 (.D(Write_Data), .en(write_en12), .clk(clk), .Q(x12_out));  // open: clr
  Register #(.width(32)) register_14 (.D(Write_Data), .en(write_en13), .clk(clk), .Q(x13_out));  // open: clr
  Register #(.width(32)) register_15 (.D(Write_Data), .en(write_en14), .clk(clk), .Q(x14_out));  // open: clr
  Register #(.width(32)) register_16 (.D(Write_Data), .en(write_en15), .clk(clk), .Q(x15_out));  // open: clr
  Register #(.width(32)) register_17 (.D(Write_Data), .en(write_en16), .clk(clk), .Q(x16_out));  // open: clr
  Register #(.width(32)) register_18 (.D(Write_Data), .en(write_en17), .clk(clk), .Q(x17_out));  // open: clr
  Register #(.width(32)) register_19 (.D(Write_Data), .en(write_en18), .clk(clk), .Q(x18_out));  // open: clr
  Register #(.width(32)) register_20 (.D(Write_Data), .en(write_en19), .clk(clk), .Q(x19_out));  // open: clr
  Register #(.width(32)) register_21 (.D(Write_Data), .en(write_en20), .clk(clk), .Q(x20_out));  // open: clr
  Register #(.width(32)) register_22 (.D(Write_Data), .en(write_en21), .clk(clk), .Q(x21_out));  // open: clr
  Register #(.width(32)) register_23 (.D(Write_Data), .en(write_en22), .clk(clk), .Q(x22_out));  // open: clr
  Register #(.width(32)) register_24 (.D(Write_Data), .en(write_en23), .clk(clk), .Q(x23_out));  // open: clr
  Register #(.width(32)) register_25 (.D(Write_Data), .en(write_en24), .clk(clk), .Q(x24_out));  // open: clr
  Register #(.width(32)) register_26 (.D(Write_Data), .en(write_en25), .clk(clk), .Q(x25_out));  // open: clr
  Register #(.width(32)) register_27 (.D(Write_Data), .en(write_en26), .clk(clk), .Q(x26_out));  // open: clr
  Register #(.width(32)) register_28 (.D(Write_Data), .en(write_en27), .clk(clk), .Q(x27_out));  // open: clr
  Register #(.width(32)) register_29 (.D(Write_Data), .en(write_en28), .clk(clk), .Q(x28_out));  // open: clr
  Register #(.width(32)) register_30 (.D(Write_Data), .en(write_en29), .clk(clk), .Q(x29_out));  // open: clr
  Register #(.width(32)) register_31 (.D(Write_Data), .en(write_en30), .clk(clk), .Q(x30_out));  // open: clr
  Register #(.width(32)) register_32 (.D(Write_Data), .en(write_en31), .clk(clk), .Q(x31_out));  // open: clr
  Multiplexer #(.enable("false"), .select(5), .width(32)) multiplexer_1 (
    .in0(x0_out), .in1(ra), .in2(sp), .in3(x3_out), .in4(x4_out), .in5(t0), .in6(t1), .in7(t2), .in8(s0),
    .in9(s1), .in10(a0), .in11(x11_out), .in12(x12_out), .in13(x13_out), .in14(x14_out), .in15(x15_out),
    .in16(x16_out), .in17(x17_out), .in18(x18_out), .in19(x19_out), .in20(x20_out), .in21(x21_out),
    .in22(x22_out), .in23(x23_out), .in24(x24_out), .in25(x25_out), .in26(x26_out), .in27(x27_out),
    .in28(x28_out), .in29(x29_out), .in30(x30_out), .in31(x31_out), .out(Read_Data_1), .sel(rs1));
  Multiplexer #(.enable("false"), .select(5), .width(32)) multiplexer_2 (
    .in0(x0_out), .in1(ra), .in2(sp), .in3(x3_out), .in4(x4_out), .in5(t0), .in6(t1), .in7(t2), .in8(s0),
    .in9(s1), .in10(a0), .in11(x11_out), .in12(x12_out), .in13(x13_out), .in14(x14_out), .in15(x15_out),
    .in16(x16_out), .in17(x17_out), .in18(x18_out), .in19(x19_out), .in20(x20_out), .in21(x21_out),
    .in22(x22_out), .in23(x23_out), .in24(x24_out), .in25(x25_out), .in26(x26_out), .in27(x27_out),
    .in28(x28_out), .in29(x29_out), .in30(x30_out), .in31(x31_out), .out(Read_Data_2), .sel(rs2));
  Demultiplexer #(.enable("false"), .select(5)) demultiplexer_1 (
    .out0(write_en0), .out1(write_en1), .out2(write_en2), .out3(write_en3), .out4(write_en4),
    .out5(write_en5), .out6(write_en6), .out7(write_en7), .out8(write_en8), .out9(write_en9),
    .out10(write_en10), .out11(write_en11), .out12(write_en12), .out13(write_en13), .out14(write_en14),
    .out15(write_en15), .out16(write_en16), .out17(write_en17), .out18(write_en18), .out19(write_en19),
    .out20(write_en20), .out21(write_en21), .out22(write_en22), .out23(write_en23), .out24(write_en24),
    .out25(write_en25), .out26(write_en26), .out27(write_en27), .out28(write_en28), .out29(write_en29),
    .out30(write_en30), .out31(write_en31), .in(RegWEn), .sel(rd));

  // Other names for the same wires on the sheet: read_data1[31:0] = Read_Data_1; read_data2[31:0] = Read_Data_2;
  //   read_reg1[4:0] = rs1; read_reg2[4:0] = rs2; write_en = RegWEn; write_reg[4:0] = rd; x1_out[31:0] = ra;
  //   x2_out[31:0] = sp; x5_out[31:0] = t0; x6_out[31:0] = t1; x7_out[31:0] = t2; x8_out[31:0] = s0;
  //   x9_out[31:0] = s1; x10_out[31:0] = a0

  // Notes on the sheet:
  //   INPUTS to your circuit
  //   DON'T CHANGE THE LOCATIONS OF THE INPUTS AND OUTPUTS!
  //   These are DEBUG/TEST outputs from your circuit.
  //   OUTPUTS from your circuit
endmodule
